# Fritzing sketch dcMotorEncoder (saved by Fritzing 1.0.1rc)

parts:
  L298N1 = L298N DC motor driver
  M2 = DC Motor [voltage_(max)=6V voltage_(min)=3V]
  Yumo-enc1 = YumoE6B2
  Part1 = Arduino Mega ADK (Rev3)
  HLK-PM1 = HLK-PM12 [part_number=HLK-PM12]

nets:
  N1: L298N1.OUT1, M2.pin_2
  N2: L298N1.OUT2, M2.pin_1
  N3: L298N1.12V, HLK-PM1.+Vo
  N4: L298N1.GND, HLK-PM1.-Vo
  N5: L298N1.ENA, Part1.D5_PWM
  N6: L298N1.IN1, Part1.D6_PWM
  N7: L298N1.IN2, Part1.D7_PWM
  N8: Yumo-enc1.V, Part1.5V
  N9: Yumo-enc1.A, Part1.GND
  N10: Yumo-enc1.B, Part1.D2_PWM
  N11: Yumo-enc1.Z, Part1.D3_PWM

notes:
  Left Motor
  L298N Motor Driver Board

custom parts:
  L298N DC motor driver: 2x DC motor driver with 78M05 positive voltage regulator (7..35 V) L298N: max 46 V, 2 A Set 5 V Enable jumper to enable 5 V regultor (needed for the L298N) and +5 V output at screw terminal or supply external +5 V at screw terminal Set ENA and/or ENB to +5 V to enable motor permanently or supply ENA and/or ENB with PWM signal IN1 and IN2 set rotation directory for motor A (OUT1/OUT2) IN2 and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
