# Fritzing sketch dcMotorPinout (saved by Fritzing 1.0.1rc)
breadboards: 1

parts:
  L298N1 = L298N DC motor driver
  M2 = DC Motor [voltage_(max)=6V voltage_(min)=3V]
  Part1 = Arduino Mega 2560 (Rev3)
  R1 = Rotary Potentiometer (Small) [maximum_resistance=100kΩ knob_status=50% power=0.5W package=THT]
  S1 = Pushbutton [package="[THT]"]
  R2 = Resistor [tolerance=±5% resistance=220 package="1206 [SMD]"]
  VCC1 = Battery block 9V

nets:
  N1: L298N1.OUT1, M2.pin_2
  N2: L298N1.OUT2, M2.pin_1
  N3: L298N1.12V, VCC1.+
  N4: L298N1.GND, VCC1.-
  N5: L298N1.ENA, Part1.D2_PWM
  N6: L298N1.IN1, Part1.D3_PWM
  N7: L298N1.IN2, Part1.D4_PWM
  N8: Part1.A0, R1.wiper
  N9: Part1.5V, R1.leg1, S1.Pin_3, S1.Pin_4
  N10: Part1.GND, R1.leg2, R2.Pin_0
  N11: Part1.D7_PWM, S1.Pin_1, S1.Pin_2, R2.Pin_1

notes:
  Left Motor
  L298N Motor Driver Board

custom parts:
  L298N DC motor driver: 2x DC motor driver with 78M05 positive voltage regulator (7..35 V) L298N: max 46 V, 2 A Set 5 V Enable jumper to enable 5 V regultor (needed for the L298N) and +5 V output at screw terminal or supply external +5 V at screw terminal Set ENA and/or ENB to +5 V to enable motor permanently or supply ENA and/or ENB with PWM signal IN1 and IN2 set rotation directory for motor A (OUT1/OUT2) IN2 and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
